# Fritzing sketch LCD Raspberry Pi (saved by Fritzing 0.9.3b)
breadboards: 1

parts:
  Raspberry_Pi_1 = Raspberry Pi 3 [part_number=RPI-3-V1.2]
  LCD1 = LCD screen
  U1 = POT [package=pot_mammoth]

nets:
  N1: Raspberry_Pi_1.GIPO21, LCD1.DB7
  N2: Raspberry_Pi_1.GIPO20, LCD1.DB6
  N3: Raspberry_Pi_1.GIPO16, LCD1.DB5
  N4: Raspberry_Pi_1.GIPO12, LCD1.DB4
  N5: Raspberry_Pi_1.GIPO23, LCD1.E
  N6: Raspberry_Pi_1.GIPO18, LCD1.RS
  GND: Raspberry_Pi_1.GND, LCD1.VSS, LCD1.R/W, LCD1.LED-, U1.E
  5V: Raspberry_Pi_1.5V, LCD1.VDD, LCD1.LED+, U1.S
  N7: LCD1.V0, U1.A
