# Fritzing sketch Catraca Inferior (saved by Fritzing 0.9.3b)

parts:
  J1 = female pin header, 1 pin [form="♀ (female)"]
  J2 = female pin header, 1 pin [form="♀ (female)"]
  J3 = female pin header, 1 pin [form="♀ (female)"]
  J4 = female pin header, 1 pin [form="♀ (female)"]
  J5 = female pin header, 1 pin [form="♀ (female)"]
  J6 = female pin header, 1 pin [form="♀ (female)"]
  J7 = female pin header, 1 pin [form="♀ (female)"]
  S1 = Pushbutton [package="[SMD]"]
  J8 = screw terminal, 3 pins
  J9 = female pin header, 3 pins [form="♀ (female)"]
  J10 = female pin header, 2 pins [form="♀ (female)"]
  J11 = female pin header, 7 pins [form="♀ (female)"]
  Part1 = Lithium Ion Polymer Battery 3.7v 1200mAh [part_number=258]
  Part2 = DB37F
  J12 = female pin header, 2 pins [form="♀ (female)"]
  J13 = female pin header, 5 pins [form="♀ (female)"]  # not connected
  J14 = female pin header, 3 pins [form="♀ (female)"]
  J15 = female pin header, 7 pins [form="♀ (female)"]
  J16 = female pin header, 6 pins [form="♀ (female)"]
  J17 = female pin header, 3 pins [form="♀ (female)"]
  LED1 = LED - 5mm [color="Green (570nm)" package="5 mm [THT]"]
  J18 = female pin header, 1 pin [form="♀ (female)"]
  J19 = female pin header, 4 pins [form="♀ (female)"]

nets:
  N1: J1.pin1, J8.pin1
  N2: J2.pin1, S1.Pin_1, S1.Pin_2, J8.pin3
  N3: J3.pin1, J8.pin2
  N4: J4.pin1, Part2.pin4, J12.pin1, LED1.cathode
  N5: J5.pin1, J9.pin2
  N6: J6.pin1, Part2.pin3, J12.pin2, LED1.anode
  N7: J7.pin1, J9.pin1, J9.pin3
  N8: S1.Pin_3, S1.Pin_4, J10.pin2, Part1.positive
  N9: J10.pin1, Part1.negative
  N10: J11.pin1, Part2.pin9
  N11: J11.pin2, Part2.pin8
  N12: J11.pin3, Part2.pin7
  N13: J11.pin4, Part2.pin6
  N14: J11.pin5, Part2.pin5
  N15: J11.pin6, Part2.pin2
  N16: J11.pin7, Part2.pin1
  N17: Part2.pin11, J15.pin1
  N18: Part2.pin12, J15.pin2
  N19: Part2.pin13, J15.pin3
  N20: Part2.pin14, J15.pin4
  N21: Part2.pin15, J15.pin5
  N22: Part2.pin16, J15.pin6
  N23: Part2.pin17, J15.pin7
  N24: Part2.pin18, J16.pin1
  N25: Part2.pin19, J16.pin2
  N26: Part2.pin20, J17.pin3
  N27: Part2.pin21, J17.pin2
  N28: Part2.pin22, Part2.pin_30, J18.pin1
  N29: Part2.pin23, J17.pin1
  N30: Part2.pin25, J19.pin4
  N31: Part2.pin_26, J19.pin3
  N32: Part2.pin_27, J19.pin2
  N33: Part2.pin_28, J19.pin1
  N34: Part2.pin_29, J16.pin6
  N35: Part2.pin_31, J14.pin2
  N36: Part2.pin_32, J14.pin3

notes:
  Power Supply
  MS-100-12
  Input: 100-240VAC - 2,5A
  Output: 12VDC - 8,5A
  Entrada
  127/220V - AC
  VTN0355
  Bateria
  12V - 1.3 Ah
  Relês - Inferior
  Sobe parte superior
  Interface de Rede

custom parts:
  Lithium Ion Polymer Battery 3.7v 1200mAh: Lithium ion polymer (also known as 'lipo' or 'lipoly') batteries are thin, light and powerful. The output ranges from 4.2V when completely charged to 3.7V. This battery has a capacity of 1200mAh for a total of about 4.5 Wh. The batteries come pre-attached with a genuine 2-pin JST-PH connector as shown and include the necessary protection circuitry.
