# Fritzing sketch Catraca Superior (saved by Fritzing 0.9.3b)

parts:
  J1 = female pin header, 3 pins [form="♀ (female)"]  # not connected
  J2 = female pin header, 2 pins [form="♀ (female)"]
  J3 = female pin header, 3 pins [form="♀ (female)"]  # not connected
  J4 = female pin header, 3 pins [form="♀ (female)"]  # not connected
  F1 = Fan - Ventilador [package=THT]
  J5 = female pin header, 2 pins [form="♀ (female)"]
  J6 = female pin header, 3 pins [form="♀ (female)"]
  L1 = Solenoid
  U1 = SWITCH_SPDT [package=kps-1290]
  Part1 = RFID-RC522-v3
  Part2 = RFID-RC522-v3
  Part3 = RFID-RC522-v3
  J8 = female pin header, 7 pins [form="♀ (female)"]
  J9 = female pin header, 7 pins [form="♀ (female)"]
  J10 = female pin header, 7 pins [form="♀ (female)"]
  J11 = female pin header, 2 pins [form="♀ (female)"]
  J13 = female pin header, 4 pins [form="♀ (female)"]  # not connected
  J14 = female pin header, 1 pin [form="♀ (female)"]
  J15 = female pin header, 1 pin [form="♀ (female)"]
  J16 = female pin header, 1 pin [form="♀ (female)"]  # not connected
  J17 = female pin header, 1 pin [form="♀ (female)"]  # not connected
  J18 = female pin header, 1 pin [form="♀ (female)"]  # not connected
  J19 = female pin header, 1 pin [form="♀ (female)"]  # not connected
  J20 = female pin header, 1 pin [form="♀ (female)"]  # not connected
  J21 = female pin header, 1 pin [form="♀ (female)"]  # not connected
  L2 = Solenoid
  J12 = female pin header, 3 pins [form="♀ (female)"]  # not connected
  L3 = Solenoid  # not connected
  Part4 = DB37F
  J22 = female pin header, 4 pins [form="♀ (female)"]
  J23 = female pin header, 4 pins [form="♀ (female)"]
  J25 = female pin header, 8 pins [form="♀ (female)"]
  J26 = female pin header, 7 pins [form="♀ (female)"]
  J27 = female pin header, 8 pins [form="♀ (female)"]
  J24 = female pin header, 8 pins [form="♀ (female)"]
  J7 = female pin header, 2 pins [form="♀ (female)"]

nets:
  GND: J2.pin1, F1.GND, L1.pin1, Part1.GND, Part2.GND, Part3.GND, J11.pin2, Part4.pin2, J7.pin2
  3.3V: J2.pin2, F1.5V, J6.pin3, Part1.3.3V, Part2.3.3V, Part3.3.3V, J11.pin1, Part4.pin1, J7.pin1
  N1: J5.pin1, U1.P
  N2: J5.pin2, U1.O
  N3: J6.pin1, L1.pin2
  N4: Part1.SDA, J8.pin4
  N5: Part1.MISO, J8.pin3
  N6: Part2.SDA, J9.pin4
  N7: Part2.MISO, J9.pin3
  N8: Part3.SDA, J10.pin4
  N9: Part3.MISO, J10.pin3
  N10: J14.pin1, L2.pin2
  N11: J15.pin1, L2.pin1
  N12: Part4.pin3, J24.pin1
  N13: Part4.pin4, J24.pin2
  N14: Part4.pin5, J24.pin3
  N15: Part4.pin6, J24.pin4
  N16: Part4.pin7, J24.pin5
  N17: Part4.pin8, J24.pin6
  N18: Part4.pin9, J24.pin7
  N19: Part4.pin11, J26.pin1
  N20: Part4.pin12, J26.pin2
  N21: Part4.pin13, J26.pin3
  N22: Part4.pin14, J26.pin4
  N23: Part4.pin15, J26.pin5
  N24: Part4.pin18, J26.pin6
  N25: Part4.pin19, J26.pin7
  N26: Part4.pin_29, J23.pin1
  N27: Part4.pin_30, J23.pin2
  N28: Part4.pin_31, J23.pin3
  N29: Part4.pin_32, J23.pin4
  N30: Part4.pin_34, J22.pin1
  N31: Part4.pin_35, J22.pin2
  N32: Part4.pin_36, J22.pin3
  N33: Part4.pin_37, J22.pin4
  N34: J25.pin1, J27.pin2
  N35: J25.pin2, J27.pin3
  N36: J25.pin3, J27.pin4
  N37: J25.pin4, J27.pin1
  N38: J25.pin5, J27.pin5
  N39: J25.pin6, J27.pin6
  N40: J25.pin7, J27.pin7
  N41: J25.pin8, J27.pin8

notes:
  Vem da parte inferior
  - Preto -
  - Azul (Giro A.H.)
  - Verde (Giro Hor.)
  Inferior - Pino 4
  Inferior - Pino 3
  12V DC
  Sensor Giro Horário
  - Marrom +
  - Azul -
  - Preto (sinal)
  12v - Detecção
  Sensor Giro Anti-Horário
  - Marrom +
  - Azul -
  - Preto (sinal)
  12v - Detecção
  Solenoide - Emergência
  Leitor 1
  (Saída)
  Leitor 2
  (Entrada)
  Leitor 3
  (Cofre)
  Inferior - Pino 3
  Inferior - Pino 4
  12V DC
  Sensor Passagem A
  Sensor Passagem B
  Relê Cofre
  Solenoide Cofre
  Inferior - Pino 31
  Inferior - Pino 32
  PT - Inferior - Pino 4
  VM - Inferior - Pino 3
  12V DC
  Solenoide - Giro
  Inferior - Pino 29
  Inferior - Pino 30
  Pictograma
  Teclado

custom parts:
  Fan - Ventilador: Ventilador de 2 pines, se encuentra comunmente en computadoras de escritorio
  RFID-RC522-v3: A simple China made RFID-RC522 Reader (6x4 cm); do check the pin labels, as this is a MFRC522 based clone.
